# Fritzing sketch led-vorwiderstand-taster (saved by Fritzing 0.9.3b)
breadboards: 1

parts:
  Part1 = Arduino Nano (Rev3.0)
  LED1 = LED - 5mm [color="Red (633nm)" package="5 mm [THT]"]
  R1 = Resistor [tolerance=±5% resistance=220 package=THT]
  S1 = Pushbutton [package="[THT]"]
  R2 = Resistor [tolerance=±5% resistance=27k package=THT]

nets (from the breadboard view):
  N1: Part1.GND, LED1.cathode, R2.Pin_1
  N2: Part1.D10, R1.Pin_1
  N3: Part1.D11/MOSI, S1.Pin_3, S1.Pin_4, R2.Pin_0
  N4: LED1.anode, R1.Pin_0
  N5: S1.Pin_1, S1.Pin_2
