# Fritzing sketch poti-buzzer (saved by Fritzing 0.9.3b)
breadboards: 1

parts:
  Part1 = Arduino Nano (Rev3.0)
  R1 = Trimmer Potentiometer [maximum_resistance=10kΩ package=THT]
  J1 = Piezo Speaker

nets:
  N1: Part1.GND, R1.leg2, J1.pin1
  N2: Part1.D10, J1.pin2
  N3: Part1.5V, R1.leg1
  N4: Part1.A3, R1.wiper
